# Fritzing sketch 2WD Arduino robot with 2xHC-SRO4 (saved by Fritzing 0.9.3b)

parts:
  Часть1 = Arduino Uno (Rev3) - ICSP
  Часть2 = Bluetooth HC-05 Macho
  Left_US_sensor = hc-sr04
  Right_US_sensor = hc-sr04
  Left_motor = DC Motor
  /Forward_direction\ = Piezo Speaker
  LED1 = LEDs [package=led10mm]
  R1 = Resistor [tolerance=±5% resistance=220 package=THT]
  U1 = L9110 H-bridge module [part_number="L9110 H-bridge"]
  VCC1 = Battery block 9V
  Right_motor = DC Motor
  U2 = SWITCH_SPDT [package=kps-1290]
  J3 = Power Plug

nets:
  N1: Часть1.D8, Right_US_sensor.Trig
  N2: Часть1.D9_PWM, U1.A-IA
  N3: Часть1.D10_PWM/SS, U1.A-IB
  N4: Часть1.D11_PWM/MOSI, Left_US_sensor.Echo
  N5: Часть1.D12/MISO, Left_US_sensor.Trig
  GND: Часть1.GND, Часть2.GND, Left_US_sensor.GND, Right_US_sensor.GND, /Forward_direction\.pin1, LED1.C, U1.GND, VCC1.-, J3.GND, J3.tip_GND
  N6: Часть1.D0/RX, Часть2.TXD
  N7: Часть1.D1/TX, Часть2.RXD
  N8: Часть1.D3_PWM, /Forward_direction\.pin2
  N9: Часть1.D4, R1.Pin_1
  N10: Часть1.D5_PWM, U1.B-IA
  N11: Часть1.D6_PWM, U1.B-IB
  N12: Часть1.D7, Right_US_sensor.Echo
  VCC: Часть1.5V, Часть2.VCC, Left_US_sensor.VCC, Right_US_sensor.VCC
  N13: Left_motor.pin_1, U1.MOTOR_A-B
  N14: Left_motor.pin_2, U1.MOTOR_A-A
  N15: LED1.A, R1.Pin_0
  N16: U1.VCC, U2.P, J3.PWR, J3.tip_PWR
  N17: U1.MOTOR_B-A, Right_motor.pin_2
  N18: U1.MOTOR_B-B, Right_motor.pin_1
  N19: VCC1.+, U2.O

custom parts:
  Power Plug: Power Jack This is the standard 5.5mm barrel plug for power. This part has bendable leads (i.e. wires in the real world) to connect to wall warts or the breadboard in the standard wire end, and hidden connectors on the tip end that will connect when "plugged in" (overlapped with the jack so it appears "plugged in" in breadboard) to the modified coax jack part. Internal busses connect the two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
